// Logisim project macro circutios.circ as structural Verilog: 1 circuit, main circuit main
module main (
  input  A3,
  input  B3,
  input  A2,
  input  B2,
  input  A1,
  input  B1,
  input  A0,
  input  B0,
  output Vai_1,
  output R,
  output R_2,
  output R_3,
  output R_4
);

  wire main_2_vai_um, main_3_vai_um, main_4_vai_um;

  somador_de_1_bit_certo_main main_1 (.A(A3), .B(B3), .Vem_um(main_2_vai_um), .R1(R), .vai_um(Vai_1));
  somador_de_1_bit_certo_main main_2 (.A(A2), .B(B2), .Vem_um(main_3_vai_um), .R1(R_2), .vai_um(main_2_vai_um));
  somador_de_1_bit_certo_main main_3 (.A(A1), .B(B1), .Vem_um(main_4_vai_um), .R1(R_3), .vai_um(main_3_vai_um));
  somador_de_1_bit_certo_main main_4 (.A(A0), .B(B0), .Vem_um(1'b0), .R1(R_4), .vai_um(main_4_vai_um));
endmodule
